// Logisim project imm-gen.circ as structural Verilog: 1 circuit, main circuit imm_gen
module imm_gen (
  input  [31:0] inst,
  input  [2:0] ImmSel,
  output [31:0] imm
);

  wire [31:0] B, bit_extender_4_out, I, J, S, U;

  assign I = {{20{1'b0}}, {12{1'b0}}};  // Bit_Extender bit_extender_1
  assign S = {{20{1'b0}}, {12{1'b0}}};  // Bit_Extender bit_extender_2
  assign B = {{20{1'b0}}, {12{1'b0}}};  // Bit_Extender bit_extender_3
  assign bit_extender_4_out = {{12{1'b0}}, {20{1'b0}}};  // Bit_Extender bit_extender_4
  assign J = {{11{1'b0}}, {21{1'b0}}};  // Bit_Extender bit_extender_5
  Multiplexer #(.enable("false"), .select(3), .width(32)) multiplexer_1 (
    .in0(I), .in1(S), .in2(B), .in3(U), .in4(J), .out(imm), .sel(ImmSel));  // open: in5, in6, in7
  Shifter #(.width(32)) shifter_1 (.in(bit_extender_4_out), .\dist (5'b01100), .out(U));
  // also tied to GND on the sheet: {imm[0], imm[1], imm[2], imm[3], imm[4], imm[5], imm[6], imm[7], imm[8], imm[9], imm[10], imm[11], imm[12], imm[13], imm[14], imm[15], imm[16], imm[17], imm[18], imm[19], imm[20], imm[21], imm[22], imm[23], imm[24], imm[25], imm[26], imm[27], imm[28], imm[29], imm[30], imm[31]}

  // Notes on the sheet:
  //   INPUTS to your circuit
  //   DON'T CHANGE THE LOCATIONS OF THE INPUTS AND OUTPUTS!
  //   OUTPUT from your circuit
endmodule
